# Fritzing sketch full breadboard (saved by Fritzing 0.9.3b)
breadboards: 3

parts:
  S1 = Pushbutton [package="[THT]"]
  S2 = Pushbutton [package="[THT]"]
  S3 = Pushbutton [package="[THT]"]
  S4 = Pushbutton [package="[THT]"]
  S5 = Pushbutton [package="[THT]"]
  S6 = Pushbutton [package="[THT]"]
  S7 = Pushbutton [package="[THT]"]
  S8 = Pushbutton [package="[THT]"]
  U1 = POT [package=pot_alpha_rv16af-20]  # not connected
  U2 = POT [package=pot_alpha_rv16af-20]  # not connected
  U3 = POT [package=pot_alpha_rv16af-20]  # not connected
  U4 = POT [package=pot_alpha_rv16af-20]  # not connected
  U5 = POT [package=pot_alpha_rv16af-20]  # not connected
  IC1 = IC, DIP package, 16 pins [chip_label=CD4051BE]  # not connected
  IC2 = IC, DIP package, 16 pins [chip_label=CD4051BE]  # not connected
  IC3 = IC, DIP package, 16 pins [chip_label=CD4051BE]  # not connected
  IC4 = IC, DIP package, 16 pins [chip_label=CD4051BE]  # not connected
  IC5 = IC, DIP package, 16 pins [chip_label=CD4051BE]  # not connected
  U6 = MIDI_CONN_FEMALE_SUPPORT [package=din_5_female_support]  # not connected
  Teensy_3_1 = Teensy 3.1  # not connected
  LED1 = LED - 5mm [color="Red (633nm)" package="5 mm [THT]"]  # not connected

nets:
  N1: S1.Pin_1, S1.Pin_2
  N2: S1.Pin_3, S1.Pin_4
  N3: S2.Pin_1, S2.Pin_2
  N4: S2.Pin_3, S2.Pin_4
  N5: S3.Pin_1, S3.Pin_2
  N6: S3.Pin_3, S3.Pin_4
  N7: S4.Pin_1, S4.Pin_2
  N8: S4.Pin_3, S4.Pin_4
  N9: S5.Pin_1, S5.Pin_2
  N10: S5.Pin_3, S5.Pin_4
  N11: S6.Pin_1, S6.Pin_2
  N12: S6.Pin_3, S6.Pin_4
  N13: S7.Pin_1, S7.Pin_2
  N14: S7.Pin_3, S7.Pin_4
  N15: S8.Pin_1, S8.Pin_2
  N16: S8.Pin_3, S8.Pin_4
